// Logisim project CRC.circ as structural Verilog: 2 circuits, main circuit CRC
module CRC (
  input  [7:0] \_8位原数据帧 ,
  input  [3:0] \_4位除数 ,
  output [10:0] \CRC校验码 
);

  wire [3:1] \n4位模二除法器_1__3位余数 , \n4位模二除法器_2__3位余数 , \n4位模二除法器_3__3位余数 , \n4位模二除法器_4__3位余数 ,
       \n4位模二除法器_5__3位余数 , \n4位模二除法器_6__3位余数 , \n4位模二除法器_7__3位余数 ;

  \_4位模二除法器  \u_4位模二除法器_1  (.\_4位被除数 (\_8位原数据帧 [7:4]), .\_4位除数 (\_4位除数 ), .\_3位余数 (\n4位模二除法器_1__3位余数 ));  // open: _1位商
  \_4位模二除法器  \u_4位模二除法器_2  (
    .\_4位被除数 ({\n4位模二除法器_1__3位余数 , \_8位原数据帧 [3]}), .\_4位除数 (\_4位除数 ), .\_3位余数 (\n4位模二除法器_2__3位余数 ));  // open: _1位商
  \_4位模二除法器  \u_4位模二除法器_3  (
    .\_4位被除数 ({\n4位模二除法器_2__3位余数 , \_8位原数据帧 [2]}), .\_4位除数 (\_4位除数 ), .\_3位余数 (\n4位模二除法器_3__3位余数 ));  // open: _1位商
  \_4位模二除法器  \u_4位模二除法器_4  (
    .\_4位被除数 ({\n4位模二除法器_3__3位余数 , \_8位原数据帧 [1]}), .\_4位除数 (\_4位除数 ), .\_3位余数 (\n4位模二除法器_4__3位余数 ));  // open: _1位商
  \_4位模二除法器  \u_4位模二除法器_5  (
    .\_4位被除数 ({\n4位模二除法器_4__3位余数 , \_8位原数据帧 [0]}), .\_4位除数 (\_4位除数 ), .\_3位余数 (\n4位模二除法器_5__3位余数 ));  // open: _1位商
  \_4位模二除法器  \u_4位模二除法器_6  (
    .\_4位被除数 ({\n4位模二除法器_5__3位余数 , 1'b0}), .\_4位除数 (\_4位除数 ), .\_3位余数 (\n4位模二除法器_6__3位余数 ));  // open: _1位商
  \_4位模二除法器  \u_4位模二除法器_7  (
    .\_4位被除数 ({\n4位模二除法器_6__3位余数 , 1'b0}), .\_4位除数 (\_4位除数 ), .\_3位余数 (\n4位模二除法器_7__3位余数 ));  // open: _1位商
  \_4位模二除法器  \u_4位模二除法器_8  (
    .\_4位被除数 ({\n4位模二除法器_7__3位余数 , 1'b0}), .\_4位除数 (\_4位除数 ), .\_3位余数 (\CRC校验码 [2:0]));  // open: _1位商

  assign \CRC校验码 [10:3] = \_8位原数据帧 ;

  // Other names for the same wires on the sheet: 除数[3:0] = \_4位除数 
endmodule

module \_4位模二除法器  (
  input  [3:0] \_4位被除数 ,
  input  [3:0] \_4位除数 ,
  output [2:0] \_3位余数 ,
  output \_1位商 
);

  wire [3:0] xor_1_out;

  assign xor_1_out = \_4位被除数  ^ \_4位除数 ;  // XOR_Gate xor_1, 4 bits wide
  BitSelector #(.width(4)) bitselector_1 (.in(\_4位被除数 ), .out(\_1位商 ), .sel(2'b11));
  Multiplexer #(.width(3)) multiplexer_1 (
    .in0(\_4位被除数 [2:0]), .in1(xor_1_out[2:0]), .out(\_3位余数 ), .sel(\_1位商 ));  // open: en
endmodule
