// Logisim project fsm.circ as structural Verilog: 3 circuits, main circuit fsm
module fsm (
  input  CLR,
  input  [1:0] In,
  output out_3
);

  wire clock_1_out;
  wire [1:0] multiplexer_1_out, register_1_q, \状态转换_1_s_ ;

  \状态转换  \u_状态转换_1  (.S(register_1_q), .In(In), .S_(\状态转换_1_s_ ));
  Multiplexer #(.width(2), .enable("false")) multiplexer_1 (
    .in0(\状态转换_1_s_ ), .in1(2'b00), .out(multiplexer_1_out), .sel(CLR));
  Register #(.width(2)) register_1 (.D(multiplexer_1_out), .Q(register_1_q), .clk(clock_1_out));  // open: en, clr
  Clock clock_1 (.out(clock_1_out));
  \状态输出  \u_状态输出_1  (.S(register_1_q), .In(In), .Z(out_3));
endmodule

module \状态转换  (
  input  [1:0] S,
  input  [1:0] In,
  output [1:0] S_
);

  wire and_1_out, and_2_out, and_3_out, and_4_out, not_1_out, not_2_out, not_3_out, not_4_out, not_5_out,
       not_6_out, not_7_out;

  not not_1 (not_1_out, S[1]);
  not not_2 (not_2_out, In[0]);
  not not_3 (not_3_out, S[0]);
  not not_4 (not_4_out, In[0]);
  not not_5 (not_5_out, In[1]);
  not not_6 (not_6_out, S[0]);
  not not_7 (not_7_out, In[0]);
  and and_1 (and_1_out, not_1_out, S[0], not_2_out);
  and and_2 (and_2_out, S[1], not_3_out, not_4_out);
  and and_3 (and_3_out, not_5_out, In[0]);
  and and_4 (and_4_out, S[1], not_6_out, not_7_out);
  or or_1 (S_[1], and_1_out, and_2_out);
  or or_2 (S_[0], and_3_out, and_4_out);
endmodule

module \状态输出  (
  input  [1:0] S,
  input  [1:0] In,
  output Z
);

  wire not_1_out, not_2_out;

  not not_1 (not_1_out, S[0]);
  not not_2 (not_2_out, In[0]);
  and and_1 (Z, S[1], not_1_out, not_2_out);
  // also tied to GND on the sheet: In[1]
endmodule
