// Logisim project ftoi.circ as structural Verilog: 3 circuits, main circuit ftoi
module ftoi (
  input  [15:0] float,
  output [31:0] \int 
);

  wire comparator_1_eq, comparator_2_eq;
  wire [31:0] multiplexer_1_out, normalized_1_out_4;

  Comparator #(.width(5), .mode("unsigned")) comparator_1 (
    .a({5{1'b1}}), .b(float[14:10]), .eq(comparator_1_eq));  // open: gt, lt
  Comparator #(.width(5), .mode("unsigned")) comparator_2 (
    .a(float[14:10]), .b({5{1'b0}}), .eq(comparator_2_eq));  // open: gt, lt
  Normalized normalized_1 (
    .sign(float[15]), .exponent(float[14:10]), .fractions(float[9:0]), .out_4(normalized_1_out_4));
  Multiplexer #(.width(32), .enable("false")) multiplexer_1 (
    .in0(normalized_1_out_4), .in1({32{1'b0}}), .out(multiplexer_1_out), .sel(comparator_2_eq));
  Multiplexer #(.width(32), .enable("false")) multiplexer_2 (
    .in0(multiplexer_1_out), .in1({32{1'b0}}), .out(\int ), .sel(comparator_1_eq));

  // Other names for the same wires on the sheet: fraction[9:0] = float[9:0]; exponent[4:0] = float[14:10];
  //   sign = float[15]
endmodule

module Normalized (
  input  sign,
  input  [4:0] exponent,
  input  [9:0] fractions,
  output [31:0] out_4
);

  wire comparator_1_lt;
  wire [4:0] exp;
  wire [31:0] bit_extender_1_out, bit_extender_2_out, multiplexer_1_out, \n32位数关于2的补码_1_out_2 , shifter_1_out;

  Subtractor #(.width(5)) subtractor_1 (.a(exponent), .b(5'b01111), .out(exp));  // open: bin, bout
  assign bit_extender_1_out = {{21{1'b0}}, {1'b1, fractions}};  // Bit_Extender bit_extender_1
  Comparator #(.width(5)) comparator_1 (.a(exp), .b({5{1'b0}}), .lt(comparator_1_lt));  // open: gt, eq
  Shifter #(.width(32)) shifter_1 (.in(bit_extender_1_out), .\dist (exp), .out(shifter_1_out));
  Multiplexer #(.width(32), .enable("false")) multiplexer_1 (
    .in0(bit_extender_2_out), .in1({32{1'b0}}), .out(multiplexer_1_out), .sel(comparator_1_lt));
  assign bit_extender_2_out = {{10{1'b0}}, shifter_1_out[31:10]};  // Bit_Extender bit_extender_2
  \_32位数关于2的补码  \u_32位数关于2的补码_1  (.\_32位数 (multiplexer_1_out), .out_2(\n32位数关于2的补码_1_out_2 ));
  Multiplexer #(.width(32), .enable("false")) multiplexer_2 (
    .in0(multiplexer_1_out), .in1(\n32位数关于2的补码_1_out_2 ), .out(out_4), .sel(sign));
endmodule

module \_32位数关于2的补码  (
  input  [31:0] \_32位数 ,
  output [31:0] out_2
);

  Subtractor #(.width(32)) subtractor_1 (.a({32{1'b0}}), .b(\_32位数 ), .out(out_2));  // open: bin, bout
endmodule
