// Logisim project grf.circ as structural Verilog: 1 circuit, main circuit grf
module grf (
  input  \clk时钟信号 ,
  input  \复位信号 ,
  input  [4:0] \读取地址A1 ,
  input  [4:0] \读取地址A2 ,
  input  [31:0] \_32位输入信号WD ,
  input  \写使能信号WE ,
  input  [4:0] \读取地址A3 ,
  output [31:0] \读取数据RD1 ,
  output [31:0] \读取数据RD2 
);

  wire [31:0] r0, r1, r2, r3, r4, r5, r6, r7, r8, r9, r10, r11, r12, r13, r14, r15, r16, r17, r18, r19, r20,
       r21, r22, r23, r24, r25, r26, r27, r28, r29, r30, r31, w0, w1, w2, w3, w4, w5, w6, w7, w8, w9, w10,
       w11, w12, w13, w14, w15, w16, w17, w18, w19, w20, w21, w22, w23, w24, w25, w26, w27, w28, w29, w30,
       w31;

  Register #(.width(32)) _0 (.D(w0), .Q(r0), .clk(\clk时钟信号 ), .clr(1'b1));  // open: en
  Register #(.width(32)) _8 (.D(w8), .Q(r8), .clk(\clk时钟信号 ), .clr(\复位信号 ));  // open: en
  Register #(.width(32)) _16 (.D(w16), .Q(r16), .clk(\clk时钟信号 ), .clr(\复位信号 ));  // open: en
  Register #(.width(32)) _24 (.D(w24), .Q(r24), .clk(\clk时钟信号 ), .clr(\复位信号 ));  // open: en
  Multiplexer #(.select(5), .width(32), .disabled(0), .enable("false")) multiplexer_1 (
    .in0(r0), .in1(r1), .in2(r2), .in3(r3), .in4(r4), .in5(r5), .in6(r6), .in7(r7), .in8(r8), .in9(r9),
    .in10(r10), .in11(r11), .in12(r12), .in13(r13), .in14(r14), .in15(r15), .in16(r16), .in17(r17),
    .in18(r18), .in19(r19), .in20(r20), .in21(r21), .in22(r22), .in23(r23), .in24(r24), .in25(r25),
    .in26(r26), .in27(r27), .in28(r28), .in29(r29), .in30(r30), .in31(r31), .out(\读取数据RD1 ), .sel(\读取地址A1 ));
  Multiplexer #(.select(5), .width(32), .disabled(0), .enable("false")) multiplexer_2 (
    .in0(r0), .in1(r1), .in2(r2), .in3(r3), .in4(r4), .in5(r5), .in6(r6), .in7(r7), .in8(r8), .in9(r9),
    .in10(r10), .in11(r11), .in12(r12), .in13(r13), .in14(r14), .in15(r15), .in16(r16), .in17(r17),
    .in18(r18), .in19(r19), .in20(r20), .in21(r21), .in22(r22), .in23(r23), .in24(r24), .in25(r25),
    .in26(r26), .in27(r27), .in28(r28), .in29(r29), .in30(r30), .in31(r31), .out(\读取数据RD2 ), .sel(\读取地址A2 ));
  Demultiplexer #(.select(5), .width(32), .tristate("true")) demultiplexer_1 (
    .out0(w0), .out1(w1), .out2(w2), .out3(w3), .out4(w4), .out5(w5), .out6(w6), .out7(w7), .out8(w8),
    .out9(w9), .out10(w10), .out11(w11), .out12(w12), .out13(w13), .out14(w14), .out15(w15), .out16(w16),
    .out17(w17), .out18(w18), .out19(w19), .out20(w20), .out21(w21), .out22(w22), .out23(w23), .out24(w24),
    .out25(w25), .out26(w26), .out27(w27), .out28(w28), .out29(w29), .out30(w30), .out31(w31),
    .in(\_32位输入信号WD ), .sel(\读取地址A3 ), .en(\写使能信号WE ));
  Register #(.width(32)) _1 (.D(w1), .Q(r1), .clk(\clk时钟信号 ), .clr(\复位信号 ));  // open: en
  Register #(.width(32)) _9 (.D(w9), .Q(r9), .clk(\clk时钟信号 ), .clr(\复位信号 ));  // open: en
  Register #(.width(32)) _17 (.D(w17), .Q(r17), .clk(\clk时钟信号 ), .clr(\复位信号 ));  // open: en
  Register #(.width(32)) _25 (.D(w25), .Q(r25), .clk(\clk时钟信号 ), .clr(\复位信号 ));  // open: en
  Register #(.width(32)) _2 (.D(w2), .Q(r2), .clk(\clk时钟信号 ), .clr(\复位信号 ));  // open: en
  Register #(.width(32)) _10 (.D(w10), .Q(r10), .clk(\clk时钟信号 ), .clr(\复位信号 ));  // open: en
  Register #(.width(32)) _18 (.D(w18), .Q(r18), .clk(\clk时钟信号 ), .clr(\复位信号 ));  // open: en
  Register #(.width(32)) _26 (.D(w26), .Q(r26), .clk(\clk时钟信号 ), .clr(\复位信号 ));  // open: en
  Register #(.width(32)) _3 (.D(w3), .Q(r3), .clk(\clk时钟信号 ), .clr(\复位信号 ));  // open: en
  Register #(.width(32)) _11 (.D(w11), .Q(r11), .clk(\clk时钟信号 ), .clr(\复位信号 ));  // open: en
  Register #(.width(32)) _19 (.D(w19), .Q(r19), .clk(\clk时钟信号 ), .clr(\复位信号 ));  // open: en
  Register #(.width(32)) _27 (.D(w27), .Q(r27), .clk(\clk时钟信号 ), .clr(\复位信号 ));  // open: en
  Register #(.width(32)) _4 (.D(w4), .Q(r4), .clk(\clk时钟信号 ), .clr(\复位信号 ));  // open: en
  Register #(.width(32)) _12 (.D(w12), .Q(r12), .clk(\clk时钟信号 ), .clr(\复位信号 ));  // open: en
  Register #(.width(32)) _20 (.D(w20), .Q(r20), .clk(\clk时钟信号 ), .clr(\复位信号 ));  // open: en
  Register #(.width(32)) _28 (.D(w28), .Q(r28), .clk(\clk时钟信号 ), .clr(\复位信号 ));  // open: en
  Register #(.width(32)) _5 (.D(w5), .Q(r5), .clk(\clk时钟信号 ), .clr(\复位信号 ));  // open: en
  Register #(.width(32)) _13 (.D(w13), .Q(r13), .clk(\clk时钟信号 ), .clr(\复位信号 ));  // open: en
  Register #(.width(32)) _21 (.D(w21), .Q(r21), .clk(\clk时钟信号 ), .clr(\复位信号 ));  // open: en
  Register #(.width(32)) _29 (.D(w29), .Q(r29), .clk(\clk时钟信号 ), .clr(\复位信号 ));  // open: en
  Register #(.width(32)) _6 (.D(w6), .Q(r6), .clk(\clk时钟信号 ), .clr(\复位信号 ));  // open: en
  Register #(.width(32)) _14 (.D(w14), .Q(r14), .clk(\clk时钟信号 ), .clr(\复位信号 ));  // open: en
  Register #(.width(32)) _22 (.D(w22), .Q(r22), .clk(\clk时钟信号 ), .clr(\复位信号 ));  // open: en
  Register #(.width(32)) _30 (.D(w30), .Q(r30), .clk(\clk时钟信号 ), .clr(\复位信号 ));  // open: en
  Register #(.width(32)) _7 (.D(w7), .Q(r7), .clk(\clk时钟信号 ), .clr(\复位信号 ));  // open: en
  Register #(.width(32)) _15 (.D(w15), .Q(r15), .clk(\clk时钟信号 ), .clr(\复位信号 ));  // open: en
  Register #(.width(32)) _23 (.D(w23), .Q(r23), .clk(\clk时钟信号 ), .clr(\复位信号 ));  // open: en
  Register #(.width(32)) _31 (.D(w31), .Q(r31), .clk(\clk时钟信号 ), .clr(\复位信号 ));  // open: en

  // Other names for the same wires on the sheet: clk = \clk时钟信号 ; reset = \复位信号 
endmodule
