// Logisim project navigation.circ as structural Verilog: 3 circuits, main circuit navigation
module navigation (
  input  [1:0] dir,
  input  clk,
  input  reset,
  output arrive,
  output hit
);

  wire \下一状态输出_1_arrive_ , \下一状态输出_1_hit_ ;
  wire [2:0] register_1_q, \状态转换_1_s_ ;

  \状态转换  \u_状态转换_1  (.S(register_1_q), .dir(dir), .S_(\状态转换_1_s_ ));
  \下一状态输出  \u_下一状态输出_1  (.S(register_1_q), .dir(dir), .arrive_(\下一状态输出_1_arrive_ ), .hit_(\下一状态输出_1_hit_ ));
  Register #(.width(3)) register_1 (.D(\状态转换_1_s_ ), .Q(register_1_q), .clk(clk), .clr(reset));  // open: en
  Register #(.width(1)) register_2 (.D(\下一状态输出_1_arrive_ ), .Q(arrive), .clk(clk), .clr(reset));  // open: en
  Register #(.width(1)) register_3 (.D(\下一状态输出_1_hit_ ), .Q(hit), .clk(clk), .clr(reset));  // open: en
endmodule

module \状态转换  (
  input  [2:0] S,
  input  [1:0] dir,
  output [2:0] S_
);

  wire and_1_out, and_2_out, and_3_out, and_4_out, and_5_out, and_6_out, and_7_out, and_8_out, and_9_out,
       and_10_out, and_11_out, not_1_out, not_2_out, not_3_out, not_4_out, not_5_out, not_6_out, not_7_out,
       not_8_out, not_9_out, not_10_out, not_11_out, not_12_out, not_13_out, not_14_out, not_15_out,
       not_16_out, not_17_out, not_18_out, not_19_out, not_20_out, not_21_out, not_22_out, not_23_out,
       not_24_out, not_25_out, not_26_out, not_27_out;

  not not_1 (not_1_out, S[2]);
  not not_2 (not_2_out, S[0]);
  not not_3 (not_3_out, dir[1]);
  not not_4 (not_4_out, dir[0]);
  not not_5 (not_5_out, S[2]);
  not not_6 (not_6_out, dir[1]);
  not not_7 (not_7_out, S[2]);
  not not_8 (not_8_out, S[1]);
  not not_9 (not_9_out, dir[1]);
  not not_10 (not_10_out, S[2]);
  not not_11 (not_11_out, dir[1]);
  not not_12 (not_12_out, dir[0]);
  not not_13 (not_13_out, S[2]);
  not not_14 (not_14_out, S[0]);
  not not_15 (not_15_out, dir[1]);
  not not_16 (not_16_out, S[2]);
  not not_17 (not_17_out, S[0]);
  not not_18 (not_18_out, dir[0]);
  not not_19 (not_19_out, S[2]);
  not not_20 (not_20_out, S[2]);
  not not_21 (not_21_out, S[1]);
  not not_22 (not_22_out, dir[1]);
  not not_23 (not_23_out, dir[0]);
  not not_24 (not_24_out, S[2]);
  not not_25 (not_25_out, S[2]);
  not not_26 (not_26_out, S[2]);
  not not_27 (not_27_out, dir[0]);
  and and_1 (and_1_out, not_1_out, S[1], not_2_out, not_3_out, not_4_out);
  and and_2 (and_2_out, not_5_out, S[1], S[0], not_6_out, dir[0]);
  and and_3 (and_3_out, not_7_out, not_8_out, S[0], not_9_out);
  and and_4 (and_4_out, not_10_out, S[0], not_11_out, not_12_out);
  and and_5 (and_5_out, not_13_out, S[1], not_14_out, not_15_out, dir[0]);
  and and_6 (and_6_out, not_16_out, S[1], not_17_out, dir[1], not_18_out);
  and and_7 (and_7_out, not_19_out, S[1], S[0], dir[1], dir[0]);
  and and_8 (and_8_out, not_20_out, not_21_out, not_22_out, not_23_out);
  and and_9 (and_9_out, not_24_out, S[0], dir[1], dir[0]);
  and and_10 (and_10_out, not_25_out, S[1], dir[1], dir[0]);
  and and_11 (and_11_out, not_26_out, S[1], S[0], not_27_out);
  or or_1 (S_[2], and_1_out, and_2_out);
  or or_2 (S_[1], and_3_out, and_4_out, and_5_out, and_6_out, and_7_out);
  or or_3 (S_[0], and_8_out, and_9_out, and_10_out, and_11_out);
endmodule

module \下一状态输出  (
  input  [2:0] S,
  input  [1:0] dir,
  output arrive_,
  output hit_
);

  wire and_1_out, and_2_out, and_3_out, and_4_out, and_5_out, and_6_out, and_7_out, not_1_out, not_2_out,
       not_3_out, not_4_out, not_5_out, not_6_out, not_7_out, not_8_out, not_9_out, not_10_out, not_11_out,
       not_12_out, not_13_out, not_14_out, not_15_out, not_16_out, not_17_out, not_18_out;

  not not_1 (not_1_out, S[2]);
  not not_2 (not_2_out, S[0]);
  not not_3 (not_3_out, dir[1]);
  not not_4 (not_4_out, S[2]);
  not not_5 (not_5_out, S[0]);
  not not_6 (not_6_out, dir[0]);
  not not_7 (not_7_out, S[2]);
  not not_8 (not_8_out, S[1]);
  not not_9 (not_9_out, S[2]);
  not not_10 (not_10_out, S[2]);
  not not_11 (not_11_out, dir[1]);
  not not_12 (not_12_out, dir[0]);
  not not_13 (not_13_out, S[2]);
  not not_14 (not_14_out, S[0]);
  not not_15 (not_15_out, dir[1]);
  not not_16 (not_16_out, dir[0]);
  not not_17 (not_17_out, S[2]);
  not not_18 (not_18_out, dir[1]);
  and and_1 (and_1_out, not_1_out, not_2_out, not_3_out, dir[0]);
  and and_2 (and_2_out, not_4_out, not_5_out, dir[1], not_6_out);
  and and_3 (and_3_out, not_7_out, not_8_out, dir[1], dir[0]);
  and and_4 (and_4_out, not_9_out, S[0], dir[1], dir[0]);
  and and_5 (and_5_out, not_10_out, S[1], S[0], not_11_out, not_12_out);
  and and_6 (and_6_out, not_13_out, S[1], not_14_out, not_15_out, not_16_out);
  and and_7 (and_7_out, not_17_out, S[1], S[0], not_18_out, dir[0]);
  or or_1 (hit_, and_1_out, and_2_out, and_3_out, and_4_out, and_5_out);
  or or_2 (arrive_, and_6_out, and_7_out);
endmodule
