// Logisim project MIPS单周期处理器（最终版）.circ as structural Verilog: 9 circuits, main circuit main
module main (
  input  reset,
  output [31:0] out_2,
  output [31:0] out_3,
  output out_4,
  output [4:0] out_5,
  output [31:0] out_6,
  output out_7,
  output [31:0] out_8,
  output [31:0] out_9
);

  wire ALUBSel, clk_out, EXTOp, Zero;
  wire [1:0] A3WRSel, NPCOp, WDSel;
  wire [2:0] ALUOp;
  wire [31:0] dm_1_rd, ext_1__32result, grf_1_rd1, multiplexer_3_out, npc_1_npc, npc_1_pc4, pc_1_a;

  Clock clk (.out(clk_out));
  NPC npc_1 (.PC(pc_1_a), .Imm(out_2[25:0]), .PC4(npc_1_pc4), .NPC(npc_1_npc), .NPCOp(NPCOp), .RS(grf_1_rd1));
  PC pc_1 (.NPC(npc_1_npc), .clk(clk_out), .reset(reset), .A(pc_1_a), .PC(out_3));
  IM im_1 (.A(pc_1_a), .OP(out_2));
  CTRL ctrl_1 (
    .opcode(out_2[31:26]), .funct(out_2[5:0]), .NPCOp(NPCOp), .ALUOp(ALUOp), .A3WRSel(A3WRSel),
    .WDSel(WDSel), .EXTOp(EXTOp), .RFWE(out_4), .ALUBSel(ALUBSel), .DMWr(out_7), .Zero(Zero));
  Multiplexer #(.select(2), .width(5), .enable("false")) multiplexer_1 (
    .in0(out_2[20:16]), .in1(out_2[15:11]), .in2({5{1'b1}}), .out(out_5), .sel(A3WRSel));  // open: in3
  Multiplexer #(.select(2), .width(32), .enable("false")) multiplexer_2 (
    .in0(out_8), .in1(dm_1_rd), .in2(npc_1_pc4), .out(out_6), .sel(WDSel));  // open: in3
  EXT ext_1 (._16input(out_2[15:0]), ._32result(ext_1__32result), .EXTOp(EXTOp));
  GRF grf_1 (
    .RD2(out_9), .readAddrA2(out_2[20:16]), .clk(clk_out), .reset(reset), ._32inWD(out_6), .RD1(grf_1_rd1),
    .readAddrA1(out_2[25:21]), .WE(out_4), .writeAddrA3(out_5));
  Multiplexer #(.width(32), .enable("false")) multiplexer_3 (
    .in0(out_9), .in1(ext_1__32result), .out(multiplexer_3_out), .sel(ALUBSel));
  ALU alu_1 (.result(out_8), .Zero(Zero), .Op1(grf_1_rd1), .Op2(multiplexer_3_out), .ALUOp(ALUOp));  // open: LessZero
  DM dm_1 (._32AddrInput(out_8), .WD(out_9), .RD(dm_1_rd), .DMWr(out_7), .clk(clk_out), .reset(reset));

  // Other names for the same wires on the sheet: DMWr = out_7; Instr[31:0] = out_2; MemAddr[31:0] = out_8;
  //   MemData[31:0] = out_9; PC[31:0] = out_3; RegAddr[4:0] = out_5; RegData[31:0] = out_6; RFWE = out_4

  // Notes on the sheet:
  //   funct
  //   imm
  //   rs
  //   rt
  //   rd
  //   imm
  //   opcode
  //   EXT_result
  //   ALU_result
  //   for_test
endmodule

module GRF (
  input  [4:0] readAddrA1,
  input  clk,
  input  reset,
  input  [31:0] _32inWD,
  input  [4:0] readAddrA2,
  input  WE,
  input  [4:0] writeAddrA3,
  output [31:0] RD1,
  output [31:0] RD2
);

  wire [31:0] r1, r2, r3, r4, r5, r6, r7, r8, r9, r10, r11, r12, r13, r14, r15, r16, r17, r18, r19, r20, r21,
       r22, r23, r24, r25, r26, r27, r28, r29, r30, r31, w0, w1, w2, w3, w4, w5, w6, w7, w8, w9, w10, w11,
       w12, w13, w14, w15, w16, w17, w18, w19, w20, w21, w22, w23, w24, w25, w26, w27, w28, w29, w30, w31;

  Register #(.width(32)) _8 (.D(w8), .Q(r8), .clk(clk), .clr(reset));  // open: en
  Register #(.width(32)) _16 (.D(w16), .Q(r16), .clk(clk), .clr(reset));  // open: en
  Register #(.width(32)) _24 (.D(w24), .Q(r24), .clk(clk), .clr(reset));  // open: en
  Register #(.width(32)) _1 (.D(w1), .Q(r1), .clk(clk), .clr(reset));  // open: en
  Register #(.width(32)) _9 (.D(w9), .Q(r9), .clk(clk), .clr(reset));  // open: en
  Register #(.width(32)) _17 (.D(w17), .Q(r17), .clk(clk), .clr(reset));  // open: en
  Register #(.width(32)) _25 (.D(w25), .Q(r25), .clk(clk), .clr(reset));  // open: en
  Demultiplexer #(.select(5), .width(32), .tristate("true")) demultiplexer_1 (
    .out0(w0), .out1(w1), .out2(w2), .out3(w3), .out4(w4), .out5(w5), .out6(w6), .out7(w7), .out8(w8),
    .out9(w9), .out10(w10), .out11(w11), .out12(w12), .out13(w13), .out14(w14), .out15(w15), .out16(w16),
    .out17(w17), .out18(w18), .out19(w19), .out20(w20), .out21(w21), .out22(w22), .out23(w23), .out24(w24),
    .out25(w25), .out26(w26), .out27(w27), .out28(w28), .out29(w29), .out30(w30), .out31(w31), .in(_32inWD),
    .sel(writeAddrA3), .en(WE));
  Register #(.width(32)) _2 (.D(w2), .Q(r2), .clk(clk), .clr(reset));  // open: en
  Register #(.width(32)) _10 (.D(w10), .Q(r10), .clk(clk), .clr(reset));  // open: en
  Register #(.width(32)) _18 (.D(w18), .Q(r18), .clk(clk), .clr(reset));  // open: en
  Register #(.width(32)) _26 (.D(w26), .Q(r26), .clk(clk), .clr(reset));  // open: en
  Register #(.width(32)) _3 (.D(w3), .Q(r3), .clk(clk), .clr(reset));  // open: en
  Register #(.width(32)) _11 (.D(w11), .Q(r11), .clk(clk), .clr(reset));  // open: en
  Register #(.width(32)) _19 (.D(w19), .Q(r19), .clk(clk), .clr(reset));  // open: en
  Register #(.width(32)) _27 (.D(w27), .Q(r27), .clk(clk), .clr(reset));  // open: en
  Register #(.width(32)) _4 (.D(w4), .Q(r4), .clk(clk), .clr(reset));  // open: en
  Register #(.width(32)) _12 (.D(w12), .Q(r12), .clk(clk), .clr(reset));  // open: en
  Register #(.width(32)) _20 (.D(w20), .Q(r20), .clk(clk), .clr(reset));  // open: en
  Register #(.width(32)) _28 (.D(w28), .Q(r28), .clk(clk), .clr(reset));  // open: en
  Register #(.width(32)) _5 (.D(w5), .Q(r5), .clk(clk), .clr(reset));  // open: en
  Register #(.width(32)) _13 (.D(w13), .Q(r13), .clk(clk), .clr(reset));  // open: en
  Register #(.width(32)) _21 (.D(w21), .Q(r21), .clk(clk), .clr(reset));  // open: en
  Register #(.width(32)) _29 (.D(w29), .Q(r29), .clk(clk), .clr(reset));  // open: en
  Register #(.width(32)) _6 (.D(w6), .Q(r6), .clk(clk), .clr(reset));  // open: en
  Register #(.width(32)) _14 (.D(w14), .Q(r14), .clk(clk), .clr(reset));  // open: en
  Register #(.width(32)) _22 (.D(w22), .Q(r22), .clk(clk), .clr(reset));  // open: en
  Register #(.width(32)) _30 (.D(w30), .Q(r30), .clk(clk), .clr(reset));  // open: en
  Register #(.width(32)) _7 (.D(w7), .Q(r7), .clk(clk), .clr(reset));  // open: en
  Register #(.width(32)) _15 (.D(w15), .Q(r15), .clk(clk), .clr(reset));  // open: en
  Register #(.width(32)) _23 (.D(w23), .Q(r23), .clk(clk), .clr(reset));  // open: en
  Register #(.width(32)) _31 (.D(w31), .Q(r31), .clk(clk), .clr(reset));  // open: en
  Multiplexer #(.select(5), .width(32), .disabled(0), .enable("false")) multiplexer_1 (
    .in0({32{1'b0}}), .in1(r1), .in2(r2), .in3(r3), .in4(r4), .in5(r5), .in6(r6), .in7(r7), .in8(r8),
    .in9(r9), .in10(r10), .in11(r11), .in12(r12), .in13(r13), .in14(r14), .in15(r15), .in16(r16), .in17(r17),
    .in18(r18), .in19(r19), .in20(r20), .in21(r21), .in22(r22), .in23(r23), .in24(r24), .in25(r25),
    .in26(r26), .in27(r27), .in28(r28), .in29(r29), .in30(r30), .in31(r31), .out(RD1), .sel(readAddrA1));
  Multiplexer #(.select(5), .width(32), .disabled(0), .enable("false")) multiplexer_2 (
    .in0({32{1'b0}}), .in1(r1), .in2(r2), .in3(r3), .in4(r4), .in5(r5), .in6(r6), .in7(r7), .in8(r8),
    .in9(r9), .in10(r10), .in11(r11), .in12(r12), .in13(r13), .in14(r14), .in15(r15), .in16(r16), .in17(r17),
    .in18(r18), .in19(r19), .in20(r20), .in21(r21), .in22(r22), .in23(r23), .in24(r24), .in25(r25),
    .in26(r26), .in27(r27), .in28(r28), .in29(r29), .in30(r30), .in31(r31), .out(RD2), .sel(readAddrA2));
endmodule

module DM (
  input  [31:0] _32AddrInput,
  input  [31:0] WD,
  input  DMWr,
  input  clk,
  input  reset,
  output [31:0] RD
);

  wire [31:0] shifter_1_out;

  Shifter #(.width(32), .shift("lr")) shifter_1 (.in(_32AddrInput), .\dist (5'b00010), .out(shifter_1_out));
  RAM #(.addrWidth(12), .dataWidth(32), .bus("separate")) ram_1 (
    .addr(shifter_1_out[11:0]), .din(WD), .data(RD), .str(DMWr), .clk(clk), .clr(reset));  // open: sel, ld
endmodule

module EXT (
  input  EXTOp,
  input  [15:0] _16input,
  output [31:0] _32result
);

  wire [31:0] bit_extender_1_out, bit_extender_2_out;

  assign bit_extender_1_out = {{16{1'b0}}, _16input};  // Bit_Extender bit_extender_1
  assign bit_extender_2_out = {{16{_16input[15]}}, _16input};  // Bit_Extender bit_extender_2
  Multiplexer #(.width(32), .enable("false")) multiplexer_1 (
    .in0(bit_extender_1_out), .in1(bit_extender_2_out), .out(_32result), .sel(EXTOp));
endmodule

module ALU (
  input  [2:0] ALUOp,
  input  [31:0] Op1,
  input  [31:0] Op2,
  output [31:0] result,
  output Zero,
  output LessZero
);

  wire [31:0] adder_1_out, or_1_out, shifter_1_out, subtractor_1_out;

  Adder #(.width(32)) adder_1 (.a(Op1), .b(Op2), .out(adder_1_out));  // open: cin, cout
  Subtractor #(.width(32)) subtractor_1 (.a(Op1), .b(Op2), .out(subtractor_1_out));  // open: bin, bout
  assign or_1_out = Op1 | Op2;  // OR_Gate or_1, 32 bits wide
  Shifter #(.width(32)) shifter_1 (.in(Op2), .\dist (5'b10000), .out(shifter_1_out));
  Comparator #(.width(32)) comparator_1 (.a(Op1), .b(Op2), .eq(Zero), .lt(LessZero));  // open: gt
  Multiplexer #(.select(3), .width(32), .enable("false")) multiplexer_1 (
    .in0(adder_1_out), .in1(subtractor_1_out), .in2(or_1_out), .in3(shifter_1_out), .out(result), .sel(ALUOp));  // open: in4, in5, in6, in7

  // Notes on the sheet:
  //   000
  //   001
  //   010
  //   011
endmodule

module PC (
  input  [31:0] NPC,
  input  clk,
  input  reset,
  output [31:0] PC,
  output [31:0] A
);

  Register #(.width(32)) register_1 (.D(NPC), .Q(A), .clk(clk), .clr(reset));  // open: en
  Adder #(.width(32)) adder_1 (.a(32'h3000), .b(A), .out(PC));  // open: cin, cout
endmodule

module NPC (
  input  [31:0] PC,
  input  [1:0] NPCOp,
  input  [25:0] Imm,
  input  [31:0] RS,
  output [31:0] PC4,
  output [31:0] NPC
);

  wire [31:0] adder_2_out, bit_extender_1_out;

  Adder #(.width(32)) adder_1 (.a(32'h4), .b(PC), .out(PC4));  // open: cin, cout
  assign bit_extender_1_out = {{14{Imm[15]}}, {Imm[15:0], 2'b00}};  // Bit_Extender bit_extender_1
  Adder #(.width(32)) adder_2 (.a(PC4), .b(bit_extender_1_out), .out(adder_2_out));  // open: cin, cout
  Multiplexer #(.select(2), .width(32), .enable("false")) multiplexer_1 (
    .in0(PC4), .in1(adder_2_out), .in2({PC[31:28], Imm, 2'b00}), .in3(RS), .out(NPC), .sel(NPCOp));

  // Notes on the sheet:
  //   00
  //   01
  //   10
  //   11
endmodule

module IM (
  input  [31:0] A,
  output [31:0] OP
);

  wire [31:0] shifter_1_out;

  Shifter #(.width(32), .shift("lr")) shifter_1 (.in(A), .\dist (5'b00010), .out(shifter_1_out));
  ROM #(.addrWidth(12), .dataWidth(32)) rom_1 (.addr(shifter_1_out[11:0]), .data(OP));  // open: sel

  // Notes on the sheet:
  //   contents of rom_1 (hex, n*v repeats v):
  //   34010001 34020002 3c03ffff 3463ffff 3c047fff 3484ffff 3c058000 34a50000 34060000 3c07ffff 34e7ffff
  //   3c08ffff 3508fffe 34090003 3c0affff 354afffd 340bffff 3c0c0001 358c0000 3c0dffff 35ad0000 3c0e1234
  //   35ce5678 3c0f8765 35ef4321 3c10c3aa 36106e53 3c117271 3631d002 3c12ffff 36520001 3c130000 36738000
  //   3c147fff 36940000 3c158000 36b50001 34167fff 34178001 3c183fff 3718ffff 3c194000 37390000 341afffe
  //   341bffff 341c1000 341d2000 341e3000 341f4000 3400007b 34080000 34090001 340a0002 340b0003 340cfffd
  //   340dfffe 340effff 340f64b3 3418a620 3419abcd 3c100000 3c110001 3c120002 3c130003 3c14fffd 3c15fffe
  //   3c16ffff 3c1764b3 12a4020 16c4820 1f85020 12d5820 18e6020 3366820 2957020 2d77820 2b6c020 9c820
  //   1008020 808820 a09020 859820 12a0020 34080000 3c090001 35290000 3c0affff 354a0000 ad0b0000 ad0c0004
  //   ad2dfff8 ad2e0008 ad4ffffc ad580000 ad590004 8d140000 8d150004 8d36fff8 8d370008 8d4bfffc 8d4c0000
  //   8d4d0004 8d000000 34040001 34050002 34060001 3c07ffff 34e7ffff 10850002 3408aaaa 8000c70 3408bbbb
  //   10860001 3409cccc 3409dddd 1084ffff 34040000 10840001 340aeeee 340affff 10a50001 340b1111 340b2222
  //   10c60002 340c3333 8000c7f 340c4444 10a60000 340d5555 10000001 340e6666 340e7777 340f0000 3418000a
  //   1e97820 11f80001 1000fffd 3419000a 327c820 13200001 1000fffd ad0f000c ad190010 ad000014 8d00000c
  //   3c10aaaa 36105555 3c115555 3631aaaa ad100018 ad11001c 8d120018 8d13001c 211a020 ad140020 3c157fff
  //   36b5ffff 2b5b020 ad160024 2a7b820 ad170028 34083039 3409d431 340adead 340bbeef 1096020 14b6820
  //   ad0c002c ad0d0030 340effff 3c0fffff 35efffff 1cec020 1e0c820 ad180034 ad190038 ad28ff9c ad2900c8
  //   8d30ff9c 8d3100c8 3412ffff 3c130000 253a020 ad14003c 34157fff 34168000 2b6b820 ad170040 2a74020
  //   ad080044 34090005 1274820 11200001 1000fffd ad090048 ad2aff38 8d4b0064 ac0c2ffc 8c0d2ffc ac0e0000
  //   8c0f0000 ac182ffc 8c192ffc 34100001 34110002 12110001 3412aaaa 12310001 3413bbbb 34140003 287a020
  //   12800001 1231fffd ad14004c
endmodule

module CTRL (
  input  [5:0] opcode,
  input  [5:0] funct,
  input  Zero,
  output [1:0] NPCOp,
  output [2:0] ALUOp,
  output [1:0] A3WRSel,
  output [1:0] WDSel,
  output EXTOp,
  output RFWE,
  output ALUBSel,
  output DMWr
);

  wire add_out, and_1_out, beq_out, jal_out, jr_out, lui_out, lw_out, nop_out, not_1_out, not_2_out,
       not_3_out, not_4_out, not_5_out, not_6_out, not_7_out, not_8_out, not_9_out, ori_out, sub_out, sw_out;

  not not_1 (not_1_out, opcode[5]);
  not not_2 (not_2_out, opcode[4]);
  not not_3 (not_3_out, opcode[3]);
  not not_4 (not_4_out, opcode[1]);
  not not_5 (not_5_out, opcode[2]);
  not not_6 (not_6_out, opcode[0]);
  not not_7 (not_7_out, funct[1]);
  not not_8 (not_8_out, funct[5]);
  not not_9 (not_9_out, funct[3]);
  and add (add_out, not_7_out, funct[5], not_6_out, not_4_out, not_5_out, not_3_out, not_2_out, not_1_out);
  and sub (sub_out, funct[1], funct[5], not_6_out, not_4_out, not_5_out, not_3_out, not_2_out, not_1_out);
  and ori (ori_out, opcode[0], not_4_out, opcode[2], opcode[3], not_2_out, not_1_out);
  and lw (lw_out, opcode[0], opcode[1], not_5_out, not_3_out, not_2_out, opcode[5]);
  and sw (sw_out, opcode[0], opcode[1], not_5_out, opcode[3], not_2_out, opcode[5]);
  and beq (beq_out, not_6_out, not_4_out, opcode[2], not_3_out, not_2_out, not_1_out);
  and lui (lui_out, opcode[0], opcode[1], opcode[2], opcode[3], not_2_out, not_1_out);
  and nop (nop_out, not_7_out, not_8_out, not_6_out, not_4_out, not_5_out, not_3_out, not_2_out, not_1_out);
  and jal (jal_out, opcode[0], opcode[1], not_5_out, not_3_out, not_2_out, not_1_out);
  and jr (jr_out, funct[3], not_6_out, not_4_out, not_5_out, not_3_out, not_2_out, not_1_out);
  or or_1 (NPCOp[1], 1'b0, jal_out, jr_out);
  and and_1 (and_1_out, beq_out, Zero);
  or or_2 (NPCOp[0], 1'b0, and_1_out, jr_out);
  or or_3 (ALUOp[1], 1'b0, ori_out, lui_out);
  buf or_4 (ALUOp[2], 1'b0);  // OR_Gate
  or or_5 (ALUOp[0], 1'b0, sub_out, beq_out, lui_out);
  or or_6 (A3WRSel[1], 1'b0, jal_out);
  or or_7 (A3WRSel[0], add_out, sub_out);
  or or_8 (WDSel[0], 1'b0, lw_out);
  or or_9 (WDSel[1], 1'b0, jal_out);
  or or_10 (EXTOp, 1'b0, lw_out, sw_out);
  or or_11 (ALUBSel, 1'b0, ori_out, lw_out, sw_out, lui_out);
  or or_12 (RFWE, jal_out, add_out, sub_out, ori_out, lw_out, lui_out);
  buf or_13 (DMWr, sw_out);  // OR_Gate

  // Other names for the same wires on the sheet: op0 = opcode[0]; op1 = opcode[1]; op2 = opcode[2]; op3 = opcode[3];
  //   op4 = opcode[4]; op5 = opcode[5]
endmodule
