// Logisim project P3_L8_behlbal_2023.circ as structural Verilog: 10 circuits, main circuit main
module main (
  input  reset,
  output [31:0] out_2,
  output [31:0] out_3,
  output out_4,
  output [4:0] out_5,
  output [31:0] out_6,
  output out_7,
  output [31:0] out_8,
  output [31:0] out_9
);

  wire ALUBSel, and_1_out, behlbal, beRFWr, clk_out, EXTOp, Zero;
  wire [1:0] A3WRSel, NPCOp, WDSel;
  wire [2:0] ALUOp;
  wire [31:0] dm_1_rd, ext_1__32, grf_1_out_8, multiplexer_3_out, npc_1_npc, npc_1_pc4, pc_1_a;

  Clock clk (.out(clk_out));
  NPC npc_1 (
    .PC(pc_1_a), .Imm(out_2[25:0]), .PC4(npc_1_pc4), .NPC(npc_1_npc), .Zero(Zero), .NPCOp(NPCOp),
    .behlbal(behlbal));
  PC pc_1 (.NPC(npc_1_npc), .clk(clk_out), .reset(reset), .A(pc_1_a), .PC(out_3));
  IM im_1 (.A(pc_1_a), .OP(out_2));
  CTRL ctrl_1 (
    .opcode(out_2[31:26]), .funct(out_2[5:0]), .NPCOp(NPCOp), .ALUOp(ALUOp), .A3WRSel(A3WRSel),
    .WDSel(WDSel), .EXTOp(EXTOp), .RFWE(out_4), .ALUBSel(ALUBSel), .DMWr(out_7));
  Multiplexer #(.select(2), .width(5), .enable("false")) multiplexer_1 (
    .in0(out_2[20:16]), .in1(out_2[15:11]), .in2({5{1'b1}}), .out(out_5), .sel(A3WRSel));  // open: in3
  Multiplexer #(.select(2), .width(32), .enable("false")) multiplexer_2 (
    .in0(out_8), .in1(dm_1_rd), .in2(npc_1_pc4), .out(out_6), .sel(WDSel));  // open: in3
  and and_1 (and_1_out, out_4, beRFWr);
  EXT ext_1 (._16(out_2[15:0]), ._32(ext_1__32), .EXTOp(EXTOp));
  GRF grf_1 (
    .out_9(out_9), .in_5(out_2[20:16]), .clk(clk_out), .in_3(reset), .in_4(out_6), .out_8(grf_1_out_8),
    .in_1(out_2[25:21]), .in_6(and_1_out), .in_7(out_5));
  Multiplexer #(.width(32), .enable("false")) multiplexer_3 (
    .in0(out_9), .in1(ext_1__32), .out(multiplexer_3_out), .sel(ALUBSel));
  ALU alu_1 (
    .result(out_8), .Zero(Zero), .Op1(grf_1_out_8), .Op2(multiplexer_3_out), .ALUOp(ALUOp),
    .behlbal_equal(behlbal), .beRFWr(beRFWr));  // open: LessZero
  DM dm_1 (.in_1(out_8), .WD(out_9), .RD(dm_1_rd), .DMWr(out_7), .clk(clk_out), .reset(reset));

  // Other names for the same wires on the sheet: DMWr = out_7; Instr[31:0] = out_2; MemAddr[31:0] = out_8;
  //   MemData[31:0] = out_9; PC[31:0] = out_3; RegAddr[4:0] = out_5; RegData[31:0] = out_6; RFWE = out_4

  // Notes on the sheet:
  //   funct
  //   imm
  //   rs
  //   rt
  //   rd
  //   imm
  //   opcode
  //   for_test
endmodule

module GRF (
  input  [4:0] in_1,
  input  clk,
  input  in_3,
  input  [31:0] in_4,
  input  [4:0] in_5,
  input  in_6,
  input  [4:0] in_7,
  output [31:0] out_8,
  output [31:0] out_9
);

  wire [31:0] r1, r2, r3, r4, r5, r6, r7, r8, r9, r10, r11, r12, r13, r14, r15, r16, r17, r18, r19, r20, r21,
       r22, r23, r24, r25, r26, r27, r28, r29, r30, r31, w0, w1, w2, w3, w4, w5, w6, w7, w8, w9, w10, w11,
       w12, w13, w14, w15, w16, w17, w18, w19, w20, w21, w22, w23, w24, w25, w26, w27, w28, w29, w30, w31;

  Register #(.width(32)) _8 (.D(w8), .Q(r8), .clk(clk), .clr(in_3));  // open: en
  Register #(.width(32)) _16 (.D(w16), .Q(r16), .clk(clk), .clr(in_3));  // open: en
  Register #(.width(32)) _24 (.D(w24), .Q(r24), .clk(clk), .clr(in_3));  // open: en
  Register #(.width(32)) _1 (.D(w1), .Q(r1), .clk(clk), .clr(in_3));  // open: en
  Register #(.width(32)) _9 (.D(w9), .Q(r9), .clk(clk), .clr(in_3));  // open: en
  Register #(.width(32)) _17 (.D(w17), .Q(r17), .clk(clk), .clr(in_3));  // open: en
  Register #(.width(32)) _25 (.D(w25), .Q(r25), .clk(clk), .clr(in_3));  // open: en
  Demultiplexer #(.select(5), .width(32), .tristate("true")) demultiplexer_1 (
    .out0(w0), .out1(w1), .out2(w2), .out3(w3), .out4(w4), .out5(w5), .out6(w6), .out7(w7), .out8(w8),
    .out9(w9), .out10(w10), .out11(w11), .out12(w12), .out13(w13), .out14(w14), .out15(w15), .out16(w16),
    .out17(w17), .out18(w18), .out19(w19), .out20(w20), .out21(w21), .out22(w22), .out23(w23), .out24(w24),
    .out25(w25), .out26(w26), .out27(w27), .out28(w28), .out29(w29), .out30(w30), .out31(w31), .in(in_4),
    .sel(in_7), .en(in_6));
  Register #(.width(32)) _2 (.D(w2), .Q(r2), .clk(clk), .clr(in_3));  // open: en
  Register #(.width(32)) _10 (.D(w10), .Q(r10), .clk(clk), .clr(in_3));  // open: en
  Register #(.width(32)) _18 (.D(w18), .Q(r18), .clk(clk), .clr(in_3));  // open: en
  Register #(.width(32)) _26 (.D(w26), .Q(r26), .clk(clk), .clr(in_3));  // open: en
  Register #(.width(32)) _3 (.D(w3), .Q(r3), .clk(clk), .clr(in_3));  // open: en
  Register #(.width(32)) _11 (.D(w11), .Q(r11), .clk(clk), .clr(in_3));  // open: en
  Register #(.width(32)) _19 (.D(w19), .Q(r19), .clk(clk), .clr(in_3));  // open: en
  Register #(.width(32)) _27 (.D(w27), .Q(r27), .clk(clk), .clr(in_3));  // open: en
  Register #(.width(32)) _4 (.D(w4), .Q(r4), .clk(clk), .clr(in_3));  // open: en
  Register #(.width(32)) _12 (.D(w12), .Q(r12), .clk(clk), .clr(in_3));  // open: en
  Register #(.width(32)) _20 (.D(w20), .Q(r20), .clk(clk), .clr(in_3));  // open: en
  Register #(.width(32)) _28 (.D(w28), .Q(r28), .clk(clk), .clr(in_3));  // open: en
  Register #(.width(32)) _5 (.D(w5), .Q(r5), .clk(clk), .clr(in_3));  // open: en
  Register #(.width(32)) _13 (.D(w13), .Q(r13), .clk(clk), .clr(in_3));  // open: en
  Register #(.width(32)) _21 (.D(w21), .Q(r21), .clk(clk), .clr(in_3));  // open: en
  Register #(.width(32)) _29 (.D(w29), .Q(r29), .clk(clk), .clr(in_3));  // open: en
  Register #(.width(32)) _6 (.D(w6), .Q(r6), .clk(clk), .clr(in_3));  // open: en
  Register #(.width(32)) _14 (.D(w14), .Q(r14), .clk(clk), .clr(in_3));  // open: en
  Register #(.width(32)) _22 (.D(w22), .Q(r22), .clk(clk), .clr(in_3));  // open: en
  Register #(.width(32)) _30 (.D(w30), .Q(r30), .clk(clk), .clr(in_3));  // open: en
  Register #(.width(32)) _7 (.D(w7), .Q(r7), .clk(clk), .clr(in_3));  // open: en
  Register #(.width(32)) _15 (.D(w15), .Q(r15), .clk(clk), .clr(in_3));  // open: en
  Register #(.width(32)) _23 (.D(w23), .Q(r23), .clk(clk), .clr(in_3));  // open: en
  Register #(.width(32)) _31 (.D(w31), .Q(r31), .clk(clk), .clr(in_3));  // open: en
  Multiplexer #(.select(5), .width(32), .disabled(0), .enable("false")) multiplexer_1 (
    .in0({32{1'b0}}), .in1(r1), .in2(r2), .in3(r3), .in4(r4), .in5(r5), .in6(r6), .in7(r7), .in8(r8),
    .in9(r9), .in10(r10), .in11(r11), .in12(r12), .in13(r13), .in14(r14), .in15(r15), .in16(r16), .in17(r17),
    .in18(r18), .in19(r19), .in20(r20), .in21(r21), .in22(r22), .in23(r23), .in24(r24), .in25(r25),
    .in26(r26), .in27(r27), .in28(r28), .in29(r29), .in30(r30), .in31(r31), .out(out_8), .sel(in_1));
  Multiplexer #(.select(5), .width(32), .disabled(0), .enable("false")) multiplexer_2 (
    .in0({32{1'b0}}), .in1(r1), .in2(r2), .in3(r3), .in4(r4), .in5(r5), .in6(r6), .in7(r7), .in8(r8),
    .in9(r9), .in10(r10), .in11(r11), .in12(r12), .in13(r13), .in14(r14), .in15(r15), .in16(r16), .in17(r17),
    .in18(r18), .in19(r19), .in20(r20), .in21(r21), .in22(r22), .in23(r23), .in24(r24), .in25(r25),
    .in26(r26), .in27(r27), .in28(r28), .in29(r29), .in30(r30), .in31(r31), .out(out_9), .sel(in_5));

  // Other names for the same wires on the sheet: reset = in_3
endmodule

module IFU (
  input  [31:0] NPC,
  input  clk,
  input  reset,
  output [31:0] OP
);

  wire [31:0] adder_1_out, register_1_q, shifter_1_out;

  Register #(.width(32)) register_1 (.D(NPC), .Q(register_1_q), .clk(clk), .clr(reset));  // open: en
  // Probe on adder_1_out
  Adder #(.width(32)) adder_1 (.a(32'h3000), .b(register_1_q), .out(adder_1_out));  // open: cin, cout
  Shifter #(.width(32), .shift("lr")) shifter_1 (.in(register_1_q), .\dist (5'b00010), .out(shifter_1_out));
  ROM #(.addrWidth(12), .dataWidth(32)) rom_1 (.addr(shifter_1_out[11:0]), .data(OP));  // open: sel
endmodule

module DM (
  input  [31:0] in_1,
  input  [31:0] WD,
  input  DMWr,
  input  clk,
  input  reset,
  output [31:0] RD
);

  wire [31:0] shifter_1_out;

  Shifter #(.width(32), .shift("lr")) shifter_1 (.in(in_1), .\dist (5'b00010), .out(shifter_1_out));
  RAM #(.addrWidth(12), .dataWidth(32), .bus("separate")) ram_1 (
    .addr(shifter_1_out[11:0]), .din(WD), .data(RD), .str(DMWr), .clk(clk), .clr(reset));  // open: sel, ld
endmodule

module EXT (
  input  EXTOp,
  input  [15:0] _16,
  output [31:0] _32
);

  wire [31:0] bit_extender_1_out, bit_extender_2_out;

  assign bit_extender_1_out = {{16{1'b0}}, _16};  // Bit_Extender bit_extender_1
  assign bit_extender_2_out = {{16{_16[15]}}, _16};  // Bit_Extender bit_extender_2
  Multiplexer #(.width(32), .enable("false")) multiplexer_1 (
    .in0(bit_extender_1_out), .in1(bit_extender_2_out), .out(_32), .sel(EXTOp));
endmodule

module ALU (
  input  [2:0] ALUOp,
  input  [31:0] Op1,
  input  [31:0] Op2,
  output [31:0] result,
  output Zero,
  output LessZero,
  output beRFWr,
  output behlbal_equal
);

  wire comparator_3_eq;
  wire [5:0] bitadder_1_out, bitadder_2_out;
  wire [31:0] adder_1_out, or_1_out, shifter_1_out, subtractor_1_out;

  BitAdder #(.width(32)) bitadder_1 (.in0(Op1), .out(bitadder_1_out));
  BitAdder #(.width(32)) bitadder_2 (.in0(Op2), .out(bitadder_2_out));
  Comparator #(.width(6), .mode("unsigned")) comparator_1 (
    .a(bitadder_1_out), .b(bitadder_2_out), .eq(behlbal_equal));  // open: gt, lt
  Adder #(.width(32)) adder_1 (.a(Op1), .b(Op2), .out(adder_1_out));  // open: cin, cout
  Subtractor #(.width(32)) subtractor_1 (.a(Op1), .b(Op2), .out(subtractor_1_out));  // open: bin, bout
  assign or_1_out = Op1 | Op2;  // OR_Gate or_1, 32 bits wide
  Shifter #(.width(32)) shifter_1 (.in(Op2), .\dist (5'b10000), .out(shifter_1_out));
  Comparator #(.width(32)) comparator_2 (.a(Op1), .b(Op2), .eq(Zero), .lt(LessZero));  // open: gt
  Multiplexer #(.select(3), .width(32), .enable("false")) multiplexer_1 (
    .in0(adder_1_out), .in1(subtractor_1_out), .in2(or_1_out), .in3(shifter_1_out), .out(result), .sel(ALUOp));  // open: in4, in5, in6, in7
  Comparator #(.width(3)) comparator_3 (.a(ALUOp), .b(3'b100), .eq(comparator_3_eq));  // open: gt, lt
  Multiplexer #(.enable("false")) multiplexer_2 (.in0(1'b1), .in1(behlbal_equal), .out(beRFWr), .sel(comparator_3_eq));

  // Notes on the sheet:
  //   beRFWr: pull=up
  //   000
  //   001
  //   010
  //   011
endmodule

module PC (
  input  [31:0] NPC,
  input  clk,
  input  reset,
  output [31:0] PC,
  output [31:0] A
);

  Register #(.width(32)) register_1 (.D(NPC), .Q(A), .clk(clk), .clr(reset));  // open: en
  Adder #(.width(32)) adder_1 (.a(32'h3000), .b(A), .out(PC));  // open: cin, cout
endmodule

module NPC (
  input  [31:0] PC,
  input  Zero,
  input  [1:0] NPCOp,
  input  [25:0] Imm,
  input  behlbal,
  output [31:0] PC4,
  output [31:0] NPC
);

  wire [31:0] adder_1_out, adder_2_out, bit_extender_1_out, multiplexer_1_out, multiplexer_2_out;

  Adder #(.width(32)) adder_1 (.a(PC), .b(32'h4), .out(adder_1_out));  // open: cin, cout
  assign bit_extender_1_out = {{14{Imm[15]}}, {Imm[15:0], 2'b00}};  // Bit_Extender bit_extender_1
  Adder #(.width(32)) adder_2 (.a(adder_1_out), .b(bit_extender_1_out), .out(adder_2_out));  // open: cin, cout
  Multiplexer #(.width(32), .enable("false")) multiplexer_1 (
    .in0(adder_1_out), .in1(adder_2_out), .out(multiplexer_1_out), .sel(Zero));
  Multiplexer #(.width(32), .enable("false")) multiplexer_2 (
    .in0(adder_1_out), .in1(adder_2_out), .out(multiplexer_2_out), .sel(behlbal));
  Multiplexer #(.select(2), .width(32), .enable("false")) multiplexer_3 (
    .in0(adder_1_out), .in1(multiplexer_1_out), .in2(multiplexer_2_out), .out(NPC), .sel(NPCOp));  // open: in3
  Adder #(.width(32)) adder_3 (.a(32'h3000), .b(adder_1_out), .out(PC4));  // open: cin, cout

  // Notes on the sheet:
  //   01
  //   00
endmodule

module IM (
  input  [31:0] A,
  output [31:0] OP
);

  wire [31:0] shifter_1_out;

  Shifter #(.width(32), .shift("lr")) shifter_1 (.in(A), .\dist (5'b00010), .out(shifter_1_out));
  ROM #(.addrWidth(12), .dataWidth(32)) rom_1 (.addr(shifter_1_out[11:0]), .data(OP));  // open: sel

  // Notes on the sheet:
  //   contents of rom_1 (hex, n*v repeats v):
  //   341c0000 341d0000 34013456 210820 8c010004 ac010004 3c027878 411822 3c051234 34040005 0 ac85ffff
  //   8c83ffff 10650001 1000000d 34670404 10e3000b 0 3c087777 3508ffff 80022 34001100 e65020 34080000
  //   34090001 340a0001 10a4020 1109fffe 1000ffff
endmodule

module CTRL (
  input  [5:0] opcode,
  input  [5:0] funct,
  output [1:0] NPCOp,
  output [2:0] ALUOp,
  output [1:0] A3WRSel,
  output [1:0] WDSel,
  output EXTOp,
  output RFWE,
  output ALUBSel,
  output DMWr
);

  wire add_out, behlbal_out, beq_out, lui_out, lw_out, nop_out, not_1_out, not_2_out, not_3_out, not_4_out,
       not_5_out, not_6_out, not_7_out, not_8_out, ori_out, sub_out, sw_out;

  not not_1 (not_1_out, opcode[5]);
  not not_2 (not_2_out, opcode[3]);
  not not_3 (not_3_out, opcode[4]);
  not not_4 (not_4_out, opcode[2]);
  not not_5 (not_5_out, opcode[1]);
  not not_6 (not_6_out, opcode[0]);
  not not_7 (not_7_out, funct[5]);
  not not_8 (not_8_out, funct[1]);
  and add (add_out, not_8_out, funct[5], not_6_out, not_5_out, not_4_out, not_2_out, not_3_out, not_1_out);
  and sub (sub_out, funct[1], funct[5], not_6_out, not_5_out, not_4_out, not_2_out, not_3_out, not_1_out);
  and ori (ori_out, opcode[0], not_5_out, opcode[2], opcode[3], not_3_out, not_1_out);
  and lw (lw_out, opcode[0], opcode[1], not_4_out, not_2_out, not_3_out, opcode[5]);
  and sw (sw_out, opcode[0], opcode[1], not_4_out, opcode[3], not_3_out, opcode[5]);
  and beq (beq_out, not_6_out, not_5_out, opcode[2], not_2_out, not_3_out, not_1_out);
  and lui (lui_out, opcode[0], opcode[1], opcode[2], opcode[3], not_3_out, not_1_out);
  and nop (nop_out, not_8_out, not_7_out, not_6_out, not_5_out, not_4_out, not_2_out, not_3_out, not_1_out);
  and behlbal (behlbal_out, not_6_out, opcode[1], opcode[2], opcode[3], opcode[4], opcode[5]);
  or or_1 (NPCOp[1], 1'b0, behlbal_out);
  or or_2 (NPCOp[0], 1'b0, beq_out);
  or or_3 (ALUOp[2], 1'b0, behlbal_out);
  or or_4 (ALUOp[0], 1'b0, sub_out, beq_out, lui_out);
  or or_5 (ALUOp[1], 1'b0, ori_out, lui_out);
  or or_6 (A3WRSel[0], add_out, sub_out);
  or or_7 (A3WRSel[1], 1'b0, behlbal_out);
  or or_8 (WDSel[1], 1'b0, behlbal_out);
  or or_9 (WDSel[0], 1'b0, lw_out);
  or or_10 (EXTOp, 1'b0, lw_out, sw_out);
  or or_11 (RFWE, behlbal_out, add_out, sub_out, ori_out, lw_out, lui_out);
  or or_12 (ALUBSel, 1'b0, ori_out, lw_out, sw_out, lui_out);
  buf or_13 (DMWr, sw_out);  // OR_Gate

  // Other names for the same wires on the sheet: op0 = opcode[0]; op1 = opcode[1]; op2 = opcode[2]; op3 = opcode[3];
  //   op4 = opcode[4]; op5 = opcode[5]
endmodule
