// Logisim project P3_L9_senodb_2023.circ as structural Verilog: 10 circuits, main circuit main
module main (
  input  reset,
  output [31:0] out_2,
  output [31:0] out_3,
  output out_4,
  output [4:0] out_5,
  output [31:0] out_6,
  output out_7,
  output [31:0] out_8,
  output [31:0] out_9
);

  wire A3WRSel, ALUBSel, clk_out, EXTOp, WDSel, Zero;
  wire [1:0] NPCOp;
  wire [2:0] ALUOp;
  wire [31:0] dm_1_rd, \ext_1__32位扩展结果 , \grf_1_读取数据rd1 , multiplexer_3_out, npc_1_npc, pc_1_a;

  Clock clk (.out(clk_out));
  NPC npc_1 (.PC(pc_1_a), .Imm(out_2[25:0]), .NPC(npc_1_npc), .Zero(Zero), .NPCOp(NPCOp));  // open: PC4
  PC pc_1 (.NPC(npc_1_npc), .clk(clk_out), .reset(reset), .A(pc_1_a), .PC(out_3));
  IM im_1 (.A(pc_1_a), .OP(out_2));
  CTRL ctrl_1 (
    .opcode(out_2[31:26]), .funct(out_2[5:0]), .NPCOp(NPCOp), .ALUOp(ALUOp), .A3WRSel(A3WRSel),
    .WDSel(WDSel), .EXTOp(EXTOp), .RFWE(out_4), .ALUBSel(ALUBSel), .DMWr(out_7));
  Multiplexer #(.width(5), .enable("false")) multiplexer_1 (
    .in0(out_2[20:16]), .in1(out_2[15:11]), .out(out_5), .sel(A3WRSel));
  Multiplexer #(.width(32), .enable("false")) multiplexer_2 (.in0(out_8), .in1(dm_1_rd), .out(out_6), .sel(WDSel));
  EXT ext_1 (.\_16位立即数输入 (out_2[15:0]), .\_32位扩展结果 (\ext_1__32位扩展结果 ), .EXTOp(EXTOp));
  GRF grf_1 (
    .\读取数据RD2 (out_9), .\读取地址A2 (out_2[20:16]), .\clk时钟信号 (clk_out), .\复位信号 (reset), .\_32位输入信号WD (out_6),
    .\读取数据RD1 (\grf_1_读取数据rd1 ), .\读取地址A1 (out_2[25:21]), .\写使能信号WE (out_4), .\写地址A3 (out_5));
  Multiplexer #(.width(32), .enable("false")) multiplexer_3 (
    .in0(out_9), .in1(\ext_1__32位扩展结果 ), .out(multiplexer_3_out), .sel(ALUBSel));
  ALU alu_1 (
    .result(out_8), .Zero(Zero), .Op1(\grf_1_读取数据rd1 ), .Op2(multiplexer_3_out), .ALUOp(ALUOp));  // open: LessZero
  DM dm_1 (.\_32位地址输入 (out_8), .WD(out_9), .RD(dm_1_rd), .DMWr(out_7), .clk(clk_out), .reset(reset));

  // Other names for the same wires on the sheet: DMWr = out_7; Instr[31:0] = out_2; MemAddr[31:0] = out_8;
  //   MemData[31:0] = out_9; PC[31:0] = out_3; RegAddr[4:0] = out_5; RegData[31:0] = out_6; RFWE = out_4

  // Notes on the sheet:
  //   funct
  //   imm
  //   rs
  //   rt
  //   rd
  //   imm
  //   opcode
  //   for_test
endmodule

module GRF (
  input  [4:0] \读取地址A1 ,
  input  \clk时钟信号 ,
  input  \复位信号 ,
  input  [31:0] \_32位输入信号WD ,
  input  [4:0] \读取地址A2 ,
  input  \写使能信号WE ,
  input  [4:0] \写地址A3 ,
  output [31:0] \读取数据RD1 ,
  output [31:0] \读取数据RD2 
);

  wire [31:0] r1, r2, r3, r4, r5, r6, r7, r8, r9, r10, r11, r12, r13, r14, r15, r16, r17, r18, r19, r20, r21,
       r22, r23, r24, r25, r26, r27, r28, r29, r30, r31, w0, w1, w2, w3, w4, w5, w6, w7, w8, w9, w10, w11,
       w12, w13, w14, w15, w16, w17, w18, w19, w20, w21, w22, w23, w24, w25, w26, w27, w28, w29, w30, w31;

  Register #(.width(32)) _8 (.D(w8), .Q(r8), .clk(\clk时钟信号 ), .clr(\复位信号 ));  // open: en
  Register #(.width(32)) _16 (.D(w16), .Q(r16), .clk(\clk时钟信号 ), .clr(\复位信号 ));  // open: en
  Register #(.width(32)) _24 (.D(w24), .Q(r24), .clk(\clk时钟信号 ), .clr(\复位信号 ));  // open: en
  Register #(.width(32)) _1 (.D(w1), .Q(r1), .clk(\clk时钟信号 ), .clr(\复位信号 ));  // open: en
  Register #(.width(32)) _9 (.D(w9), .Q(r9), .clk(\clk时钟信号 ), .clr(\复位信号 ));  // open: en
  Register #(.width(32)) _17 (.D(w17), .Q(r17), .clk(\clk时钟信号 ), .clr(\复位信号 ));  // open: en
  Register #(.width(32)) _25 (.D(w25), .Q(r25), .clk(\clk时钟信号 ), .clr(\复位信号 ));  // open: en
  Demultiplexer #(.select(5), .width(32), .tristate("true")) demultiplexer_1 (
    .out0(w0), .out1(w1), .out2(w2), .out3(w3), .out4(w4), .out5(w5), .out6(w6), .out7(w7), .out8(w8),
    .out9(w9), .out10(w10), .out11(w11), .out12(w12), .out13(w13), .out14(w14), .out15(w15), .out16(w16),
    .out17(w17), .out18(w18), .out19(w19), .out20(w20), .out21(w21), .out22(w22), .out23(w23), .out24(w24),
    .out25(w25), .out26(w26), .out27(w27), .out28(w28), .out29(w29), .out30(w30), .out31(w31),
    .in(\_32位输入信号WD ), .sel(\写地址A3 ), .en(\写使能信号WE ));
  Register #(.width(32)) _2 (.D(w2), .Q(r2), .clk(\clk时钟信号 ), .clr(\复位信号 ));  // open: en
  Register #(.width(32)) _10 (.D(w10), .Q(r10), .clk(\clk时钟信号 ), .clr(\复位信号 ));  // open: en
  Register #(.width(32)) _18 (.D(w18), .Q(r18), .clk(\clk时钟信号 ), .clr(\复位信号 ));  // open: en
  Register #(.width(32)) _26 (.D(w26), .Q(r26), .clk(\clk时钟信号 ), .clr(\复位信号 ));  // open: en
  Register #(.width(32)) _3 (.D(w3), .Q(r3), .clk(\clk时钟信号 ), .clr(\复位信号 ));  // open: en
  Register #(.width(32)) _11 (.D(w11), .Q(r11), .clk(\clk时钟信号 ), .clr(\复位信号 ));  // open: en
  Register #(.width(32)) _19 (.D(w19), .Q(r19), .clk(\clk时钟信号 ), .clr(\复位信号 ));  // open: en
  Register #(.width(32)) _27 (.D(w27), .Q(r27), .clk(\clk时钟信号 ), .clr(\复位信号 ));  // open: en
  Register #(.width(32)) _4 (.D(w4), .Q(r4), .clk(\clk时钟信号 ), .clr(\复位信号 ));  // open: en
  Register #(.width(32)) _12 (.D(w12), .Q(r12), .clk(\clk时钟信号 ), .clr(\复位信号 ));  // open: en
  Register #(.width(32)) _20 (.D(w20), .Q(r20), .clk(\clk时钟信号 ), .clr(\复位信号 ));  // open: en
  Register #(.width(32)) _28 (.D(w28), .Q(r28), .clk(\clk时钟信号 ), .clr(\复位信号 ));  // open: en
  Register #(.width(32)) _5 (.D(w5), .Q(r5), .clk(\clk时钟信号 ), .clr(\复位信号 ));  // open: en
  Register #(.width(32)) _13 (.D(w13), .Q(r13), .clk(\clk时钟信号 ), .clr(\复位信号 ));  // open: en
  Register #(.width(32)) _21 (.D(w21), .Q(r21), .clk(\clk时钟信号 ), .clr(\复位信号 ));  // open: en
  Register #(.width(32)) _29 (.D(w29), .Q(r29), .clk(\clk时钟信号 ), .clr(\复位信号 ));  // open: en
  Register #(.width(32)) _6 (.D(w6), .Q(r6), .clk(\clk时钟信号 ), .clr(\复位信号 ));  // open: en
  Register #(.width(32)) _14 (.D(w14), .Q(r14), .clk(\clk时钟信号 ), .clr(\复位信号 ));  // open: en
  Register #(.width(32)) _22 (.D(w22), .Q(r22), .clk(\clk时钟信号 ), .clr(\复位信号 ));  // open: en
  Register #(.width(32)) _30 (.D(w30), .Q(r30), .clk(\clk时钟信号 ), .clr(\复位信号 ));  // open: en
  Register #(.width(32)) _7 (.D(w7), .Q(r7), .clk(\clk时钟信号 ), .clr(\复位信号 ));  // open: en
  Register #(.width(32)) _15 (.D(w15), .Q(r15), .clk(\clk时钟信号 ), .clr(\复位信号 ));  // open: en
  Register #(.width(32)) _23 (.D(w23), .Q(r23), .clk(\clk时钟信号 ), .clr(\复位信号 ));  // open: en
  Register #(.width(32)) _31 (.D(w31), .Q(r31), .clk(\clk时钟信号 ), .clr(\复位信号 ));  // open: en
  Multiplexer #(.select(5), .width(32), .disabled(0), .enable("false")) multiplexer_1 (
    .in0({32{1'b0}}), .in1(r1), .in2(r2), .in3(r3), .in4(r4), .in5(r5), .in6(r6), .in7(r7), .in8(r8),
    .in9(r9), .in10(r10), .in11(r11), .in12(r12), .in13(r13), .in14(r14), .in15(r15), .in16(r16), .in17(r17),
    .in18(r18), .in19(r19), .in20(r20), .in21(r21), .in22(r22), .in23(r23), .in24(r24), .in25(r25),
    .in26(r26), .in27(r27), .in28(r28), .in29(r29), .in30(r30), .in31(r31), .out(\读取数据RD1 ), .sel(\读取地址A1 ));
  Multiplexer #(.select(5), .width(32), .disabled(0), .enable("false")) multiplexer_2 (
    .in0({32{1'b0}}), .in1(r1), .in2(r2), .in3(r3), .in4(r4), .in5(r5), .in6(r6), .in7(r7), .in8(r8),
    .in9(r9), .in10(r10), .in11(r11), .in12(r12), .in13(r13), .in14(r14), .in15(r15), .in16(r16), .in17(r17),
    .in18(r18), .in19(r19), .in20(r20), .in21(r21), .in22(r22), .in23(r23), .in24(r24), .in25(r25),
    .in26(r26), .in27(r27), .in28(r28), .in29(r29), .in30(r30), .in31(r31), .out(\读取数据RD2 ), .sel(\读取地址A2 ));

  // Other names for the same wires on the sheet: clk = \clk时钟信号 ; reset = \复位信号 
endmodule

module IFU (
  input  [31:0] NPC,
  input  clk,
  input  reset,
  output [31:0] OP
);

  wire [31:0] adder_1_out, register_1_q, shifter_1_out;

  Register #(.width(32)) register_1 (.D(NPC), .Q(register_1_q), .clk(clk), .clr(reset));  // open: en
  // Probe on adder_1_out
  Adder #(.width(32)) adder_1 (.a(32'h3000), .b(register_1_q), .out(adder_1_out));  // open: cin, cout
  Shifter #(.width(32), .shift("lr")) shifter_1 (.in(register_1_q), .\dist (5'b00010), .out(shifter_1_out));
  ROM #(.addrWidth(12), .dataWidth(32)) rom_1 (.addr(shifter_1_out[11:0]), .data(OP));  // open: sel
endmodule

module DM (
  input  [31:0] \_32位地址输入 ,
  input  [31:0] WD,
  input  DMWr,
  input  clk,
  input  reset,
  output [31:0] RD
);

  wire [31:0] shifter_1_out;

  Shifter #(.width(32), .shift("lr")) shifter_1 (.in(\_32位地址输入 ), .\dist (5'b00010), .out(shifter_1_out));
  RAM #(.addrWidth(12), .dataWidth(32), .bus("separate")) ram_1 (
    .addr(shifter_1_out[11:0]), .din(WD), .data(RD), .str(DMWr), .clk(clk), .clr(reset));  // open: sel, ld
endmodule

module EXT (
  input  EXTOp,
  input  [15:0] \_16位立即数输入 ,
  output [31:0] \_32位扩展结果 
);

  wire [31:0] bit_extender_1_out, bit_extender_2_out;

  assign bit_extender_1_out = {{16{1'b0}}, \_16位立即数输入 };  // Bit_Extender bit_extender_1
  assign bit_extender_2_out = {{16{\_16位立即数输入 [15]}}, \_16位立即数输入 };  // Bit_Extender bit_extender_2
  Multiplexer #(.width(32), .enable("false")) multiplexer_1 (
    .in0(bit_extender_1_out), .in1(bit_extender_2_out), .out(\_32位扩展结果 ), .sel(EXTOp));
endmodule

module ALU (
  input  [2:0] ALUOp,
  input  [31:0] Op1,
  input  [31:0] Op2,
  output [31:0] result,
  output Zero,
  output LessZero
);

  wire not_1_out;
  wire [5:0] bitadder_1_out, divider_1_rem;
  wire [31:0] adder_1_out, bit_extender_1_out, or_1_out, shifter_1_out, subtractor_1_out, xor_1_out;

  assign xor_1_out = Op1 ^ Op2;  // XOR_Gate xor_1, 32 bits wide
  BitAdder #(.width(32)) bitadder_1 (.in0(xor_1_out), .out(bitadder_1_out));
  Divider #(.width(6)) divider_1 (.a(bitadder_1_out), .b(6'b000010), .rem(divider_1_rem));  // open: out, upper
  not not_1 (not_1_out, divider_1_rem[0]);
  Adder #(.width(32)) adder_1 (.a(Op1), .b(Op2), .out(adder_1_out));  // open: cin, cout
  Subtractor #(.width(32)) subtractor_1 (.a(Op1), .b(Op2), .out(subtractor_1_out));  // open: bin, bout
  assign or_1_out = Op1 | Op2;  // OR_Gate or_1, 32 bits wide
  Shifter #(.width(32)) shifter_1 (.in(Op2), .\dist (5'b10000), .out(shifter_1_out));
  Comparator #(.width(32)) comparator_1 (.a(Op1), .b(Op2), .eq(Zero), .lt(LessZero));  // open: gt
  assign bit_extender_1_out = {{31{1'b0}}, not_1_out};  // Bit_Extender bit_extender_1
  Multiplexer #(.select(3), .width(32), .enable("false")) multiplexer_1 (
    .in0(adder_1_out), .in1(subtractor_1_out), .in2(or_1_out), .in3(shifter_1_out), .in4(bit_extender_1_out),
    .out(result), .sel(ALUOp));  // open: in5, in6, in7

  // Notes on the sheet:
  //   000
  //   001
  //   010
  //   011
endmodule

module PC (
  input  [31:0] NPC,
  input  clk,
  input  reset,
  output [31:0] PC,
  output [31:0] A
);

  Register #(.width(32)) register_1 (.D(NPC), .Q(A), .clk(clk), .clr(reset));  // open: en
  Adder #(.width(32)) adder_1 (.a(32'h3000), .b(A), .out(PC));  // open: cin, cout
endmodule

module NPC (
  input  [31:0] PC,
  input  Zero,
  input  [1:0] NPCOp,
  input  [25:0] Imm,
  output [31:0] PC4,
  output [31:0] NPC
);

  wire [31:0] adder_2_out, bit_extender_1_out, multiplexer_1_out;

  Adder #(.width(32)) adder_1 (.a(PC), .b(32'h4), .out(PC4));  // open: cin, cout
  assign bit_extender_1_out = {{14{Imm[15]}}, {Imm[15:0], 2'b00}};  // Bit_Extender bit_extender_1
  Adder #(.width(32)) adder_2 (.a(PC4), .b(bit_extender_1_out), .out(adder_2_out));  // open: cin, cout
  Multiplexer #(.width(32), .enable("false")) multiplexer_1 (
    .in0(PC4), .in1(adder_2_out), .out(multiplexer_1_out), .sel(Zero));
  Multiplexer #(.select(2), .width(32), .enable("false")) multiplexer_2 (
    .in0(PC4), .in1(multiplexer_1_out), .out(NPC), .sel(NPCOp));  // open: in2, in3

  // Notes on the sheet:
  //   01
  //   00
endmodule

module IM (
  input  [31:0] A,
  output [31:0] OP
);

  wire [31:0] shifter_1_out;

  Shifter #(.width(32), .shift("lr")) shifter_1 (.in(A), .\dist (5'b00010), .out(shifter_1_out));
  ROM #(.addrWidth(12), .dataWidth(32)) rom_1 (.addr(shifter_1_out[11:0]), .data(OP));  // open: sel

  // Notes on the sheet:
  //   contents of rom_1 (hex, n*v repeats v):
  //   3404007b 348501c8 3c06007b 3c07ffff 34e7ffff 868020 878820 e79020 34080000 ad040000 ad050004
  //   ad060008 ad07000c ad100010 ad110014 ad120018 8d040000 8d05000c ad04001c ad050020 34040001 34050002
  //   34060001 10850001 10860001 ad040024 3068
endmodule

module CTRL (
  input  [5:0] opcode,
  input  [5:0] funct,
  output [1:0] NPCOp,
  output [2:0] ALUOp,
  output A3WRSel,
  output WDSel,
  output EXTOp,
  output RFWE,
  output ALUBSel,
  output DMWr
);

  wire add_out, beq_out, lui_out, lw_out, nop_out, not_1_out, not_2_out, not_3_out, not_4_out, not_5_out,
       not_6_out, not_7_out, not_8_out, not_9_out, not_10_out, not_11_out, ori_out, senodb_out, sub_out,
       sw_out;

  not not_1 (not_1_out, opcode[5]);
  not not_2 (not_2_out, opcode[3]);
  not not_3 (not_3_out, opcode[4]);
  not not_4 (not_4_out, opcode[2]);
  not not_5 (not_5_out, opcode[1]);
  not not_6 (not_6_out, opcode[0]);
  not not_7 (not_7_out, funct[5]);
  not not_8 (not_8_out, funct[1]);
  not not_9 (not_9_out, funct[0]);
  not not_10 (not_10_out, funct[2]);
  not not_11 (not_11_out, funct[3]);
  and add (add_out, not_8_out, funct[5], not_6_out, not_5_out, not_4_out, not_2_out, not_3_out, not_1_out);
  and sub (sub_out, funct[1], funct[5], not_6_out, not_5_out, not_4_out, not_2_out, not_3_out, not_1_out);
  and ori (ori_out, opcode[0], not_5_out, opcode[2], opcode[3], not_3_out, not_1_out);
  and lw (lw_out, opcode[0], opcode[1], not_4_out, not_2_out, not_3_out, opcode[5]);
  and sw (sw_out, opcode[0], opcode[1], not_4_out, opcode[3], not_3_out, opcode[5]);
  and beq (beq_out, not_6_out, not_5_out, opcode[2], not_2_out, not_3_out, not_1_out);
  and lui (lui_out, opcode[0], opcode[1], opcode[2], opcode[3], not_3_out, not_1_out);
  and nop (nop_out, not_8_out, not_7_out, not_6_out, not_5_out, not_4_out, not_2_out, not_3_out, not_1_out);
  and senodb (senodb_out, funct[3], funct[2], funct[0], funct[1], not_6_out, not_5_out, not_4_out, not_2_out, not_3_out, not_1_out);
  buf or_1 (NPCOp[1], 1'b0);  // OR_Gate
  or or_2 (NPCOp[0], 1'b0, beq_out);
  or or_3 (ALUOp[1], 1'b0, ori_out, lui_out);
  or or_4 (ALUOp[2], 1'b0, senodb_out);
  or or_5 (ALUOp[0], 1'b0, sub_out, beq_out, lui_out);
  or or_6 (A3WRSel, add_out, sub_out, senodb_out);
  or or_7 (WDSel, 1'b0, lw_out);
  or or_8 (EXTOp, 1'b0, lw_out, sw_out);
  or or_9 (RFWE, add_out, sub_out, ori_out, lw_out, lui_out, senodb_out);
  or or_10 (ALUBSel, 1'b0, ori_out, lw_out, sw_out, lui_out);
  buf or_11 (DMWr, sw_out);  // OR_Gate

  // Other names for the same wires on the sheet: op0 = opcode[0]; op1 = opcode[1]; op2 = opcode[2]; op3 = opcode[3];
  //   op4 = opcode[4]; op5 = opcode[5]
endmodule
