// Logisim project 2n mod 5.circ as structural Verilog: 3 circuits, main circuit mod5
module mod5 (
  input  b,
  output S0,
  output S1,
  output S2,
  output S3,
  output S4
);

  wire clock_1_out;
  wire [1:0] register_1_q, \状态转换_c0_ ;

  \状态转换  \u_状态转换  (.b(b), .C0_(\状态转换_c0_ [0]), .C1_(\状态转换_c0_ [1]), .C0(register_1_q[0]), .C1(register_1_q[1]));
  Clock clock_1 (.out(clock_1_out));
  Register #(.width(2)) register_1 (.D(\状态转换_c0_ ), .Q(register_1_q), .clk(clock_1_out));  // open: en, clr
  \状态输出  \u_状态输出  (.C1(register_1_q[1]), .S0(S0), .C0(register_1_q[0]), .S1(S1), .b(b), .S2(S2), .S3(S3), .S4(S4));
endmodule

module \状态转换  (
  input  C1,
  input  C0,
  input  b,
  output C1_,
  output C0_
);


  assign C0_ = b;
  assign C1_ = C0;
endmodule

module \状态输出  (
  input  C1,
  input  C0,
  input  b,
  output S0,
  output S1,
  output S2,
  output S3,
  output S4
);

  wire not_1_out, not_2_out, not_3_out, not_4_out;

  not not_1 (not_1_out, C0);
  not not_2 (not_2_out, b);
  not not_3 (not_3_out, C0);
  and and_1 (S3, C0, b);
  not not_4 (not_4_out, b);
  and and_2 (S1, not_1_out, not_2_out);
  and and_3 (S2, not_3_out, b);
  and and_4 (S4, C0, not_4_out);

  assign S0 = 1'b0;
endmodule
