// Logisim project fibonacci.circ as structural Verilog: 2 circuits, main circuit main
module main (
  input  [2:0] N,
  output [3:0] Nth
);

  wire and_1_out, clk, comparator_1_eq, comparator_1_lt, comparator_2_eq, comparator_3_eq, move;
  wire [3:0] bit_extender_1_out, cnt, multiplexer_1_out, multiplexer_2_out, register_1_q, register_2_q,
       \状态转换_1_now_ , \状态转换_1_prev_ ;

  assign bit_extender_1_out = {{1{1'b0}}, N};  // Bit_Extender bit_extender_1
  Counter #(.width(4), .max('hf), .ongoal("stay")) counter_1 (.Q(cnt), .clk(clk));  // open: load, D, count, carry, clr
  Clock clock_1 (.out(clk));
  Comparator #(.width(4), .mode("unsigned")) comparator_1 (
    .a(cnt), .b(bit_extender_1_out), .eq(comparator_1_eq), .lt(comparator_1_lt));  // open: gt
  Multiplexer #(.width(4), .enable("false")) multiplexer_1 (
    .in0(register_2_q), .in1(4'b0001), .out(multiplexer_1_out), .sel(comparator_2_eq));
  Comparator #(.width(4), .mode("unsigned")) comparator_2 (.a(4'b0001), .b(cnt), .eq(comparator_2_eq));  // open: gt, lt
  Comparator #(.width(4), .mode("unsigned")) comparator_3 (.a(4'b0000), .b(cnt), .eq(comparator_3_eq));  // open: gt, lt
  Multiplexer #(.width(4), .enable("false")) multiplexer_2 (
    .in0(multiplexer_1_out), .in1(4'b0000), .out(multiplexer_2_out), .sel(comparator_3_eq));
  or or_1 (move, comparator_1_eq, comparator_1_lt);
  \状态转换  \u_状态转换_1  (.prev(register_1_q), .now(multiplexer_2_out), .prev_(\状态转换_1_prev_ ), .now_(\状态转换_1_now_ ));
  Register #(.width(4)) register_1 (.D(\状态转换_1_prev_ ), .Q(register_1_q), .clk(and_1_out));  // open: en, clr
  Register #(.width(4)) register_2 (.D(\状态转换_1_now_ ), .Q(register_2_q), .clk(and_1_out));  // open: en, clr
  and and_1 (and_1_out, move, clk);
  Multiplexer #(.width(4), .enable("false")) multiplexer_3 (.in0(register_1_q), .in1(4'b0000), .out(Nth), .sel(move));
endmodule

module \状态转换  (
  input  [3:0] prev,
  input  [3:0] now,
  output [3:0] prev_,
  output [3:0] now_
);

  Adder #(.width(4)) adder_1 (.a(prev), .b(now), .out(now_));  // open: cin, cout

  assign prev_ = now;
endmodule
