// Logisim project swap.circ as structural Verilog: 4 circuits, main circuit 1bit_swap
module _1bit_swap (
  input  I1,
  input  I2,
  input  S,
  output O1,
  output O2
);

  wire and_1_out, and_2_out, and_3_out, and_4_out, not_1_out, not_2_out;

  not not_1 (not_1_out, S);
  not not_2 (not_2_out, S);
  and and_1 (and_1_out, I2, S);
  and and_2 (and_2_out, I1, not_1_out);
  and and_3 (and_3_out, I2, not_2_out);
  and and_4 (and_4_out, I1, S);
  or or_1 (O1, and_1_out, and_2_out);
  or or_2 (O2, and_3_out, and_4_out);
endmodule

module _4bit_swap (
  input  [3:0] I1,
  input  [3:0] I2,
  input  S,
  output [3:0] O1,
  output [3:0] O2
);

  _1bit_swap u_1bit_swap_1 (.I1(I1[0]), .I2(I2[0]), .S(S), .O1(O1[0]), .O2(O2[0]));
  _1bit_swap u_1bit_swap_2 (.I1(I1[1]), .I2(I2[1]), .S(S), .O1(O1[1]), .O2(O2[1]));
  _1bit_swap u_1bit_swap_3 (.I1(I1[2]), .I2(I2[2]), .S(S), .O1(O1[2]), .O2(O2[2]));
  _1bit_swap u_1bit_swap_4 (.I1(I1[3]), .I2(I2[3]), .S(S), .O1(O1[3]), .O2(O2[3]));
endmodule

module _4bit_sort (
  input  [3:0] in_1,
  input  [3:0] in_2,
  input  [3:0] in_3,
  input  [3:0] in_4,
  output [3:0] out_5,
  output [3:0] out_6,
  output [3:0] out_7,
  output [3:0] out_8
);

  wire [3:0] if_larger_then_swap_1_o1, if_larger_then_swap_1_o2, if_larger_then_swap_2_o1,
       if_larger_then_swap_2_o2, if_larger_then_swap_3_o2, if_larger_then_swap_4_o1,
       if_larger_then_swap_4_o2, if_larger_then_swap_5_o2;

  if_larger_then_swap if_larger_then_swap_1 (
    .I1(in_1), .I2(in_2), .O1(if_larger_then_swap_1_o1), .O2(if_larger_then_swap_1_o2));
  if_larger_then_swap if_larger_then_swap_2 (
    .I1(if_larger_then_swap_1_o1), .I2(in_3), .O1(if_larger_then_swap_2_o1), .O2(if_larger_then_swap_2_o2));
  if_larger_then_swap if_larger_then_swap_3 (
    .I1(if_larger_then_swap_2_o1), .I2(in_4), .O1(out_5), .O2(if_larger_then_swap_3_o2));
  if_larger_then_swap if_larger_then_swap_4 (
    .I1(if_larger_then_swap_1_o2), .I2(if_larger_then_swap_2_o2), .O1(if_larger_then_swap_4_o1),
    .O2(if_larger_then_swap_4_o2));
  if_larger_then_swap if_larger_then_swap_5 (
    .I1(if_larger_then_swap_4_o1), .I2(if_larger_then_swap_3_o2), .O1(out_6), .O2(if_larger_then_swap_5_o2));
  if_larger_then_swap if_larger_then_swap_6 (
    .I1(if_larger_then_swap_4_o2), .I2(if_larger_then_swap_5_o2), .O1(out_7), .O2(out_8));
endmodule

module if_larger_then_swap (
  input  [3:0] I1,
  input  [3:0] I2,
  output [3:0] O1,
  output [3:0] O2
);

  wire comparator_1_gt;

  Comparator #(.width(4), .mode("unsigned")) comparator_1 (.a(I1), .b(I2), .gt(comparator_1_gt));  // open: eq, lt
  _4bit_swap u_4bit_swap_1 (.I1(I1), .I2(I2), .S(comparator_1_gt), .O1(O1), .O2(O2));
endmodule
